// Logisim project practica3.circ as structural Verilog
module SI_SOLO_SI (
  input  P,
  input  Q,
  output RESULTADO
);

  wire and_1_out, and_2_out, not_1_out, not_2_out;

  not not_1 (not_1_out, P);
  not not_2 (not_2_out, Q);
  and and_1 (and_1_out, not_1_out, not_2_out);
  and and_2 (and_2_out, P, Q);
  or or_1 (RESULTADO, and_1_out, and_2_out);
endmodule
